# Fritzing sketch SensorSolo (saved by Fritzing 0.9.2b)
breadboards: 1

parts:
  U5 = NodeMCU V3.0
  Componente1 = FC-28 Soil Hygrometer Module - Probe
  Componente2 = FC-28 Soil Hygrometer Module
  Componente3 = FC-28 Soil Hygrometer Module - Probe
  Componente4 = FC-28 Soil Hygrometer Module
  Componente5 = FC-28 Soil Hygrometer Module - Probe
  Componente6 = FC-28 Soil Hygrometer Module
  Componente7 = FC-28 Soil Hygrometer Module - Probe
  Componente8 = FC-28 Soil Hygrometer Module
  D2 = Diode [package=diode-1n4001]
  D4 = Diode [package=diode-1n4001]
  D5 = Diode [package=diode-1n4001]
  D6 = Diode [package=diode-1n4001]

nets:
  GND: U5.GND#6, U5.GND#13, U5.GND#16, U5.GND#33, Componente2.GND, Componente4.GND, Componente6.GND, Componente8.GND
  N1: U5.D5, Componente6.VCC
  N2: U5.D6, Componente4.VCC
  N3: U5.D7, Componente2.VCC
  N4: U5.D8, Componente8.VCC
  N5: U5.A0, D2.C, D4.C, D5.C, D6.C
  N6: Componente1.POS, Componente2.POS
  N7: Componente1.NEG, Componente2.NEG
  N8: Componente2.AO, D2.A
  N9: Componente3.POS, Componente4.POS
  N10: Componente3.NEG, Componente4.NEG
  N11: Componente4.AO, D5.A
  N12: Componente5.POS, Componente6.POS
  N13: Componente5.NEG, Componente6.NEG
  N14: Componente6.AO, D6.A
  N15: Componente7.POS, Componente8.POS
  N16: Componente7.NEG, Componente8.NEG
  N17: Componente8.AO, D4.A

custom parts:
  NodeMCU V3.0: ESP8266 based NodeMCU
  FC-28 Soil Hygrometer Module - Probe: The FC-28 is a soil hygrometer module that uses the Texas Instruments LM393 comparator chip to provide an analog measurement of soil humidity.
  FC-28 Soil Hygrometer Module: The FC-28 is a soil hygrometer module that uses the Texas Instruments LM393 comparator chip to provide an analog measurement of soil humidity. The digital output is high when soil moisture is over a certain threshold, as determined by adjusting the potentiometer.
